// Logisim project projetoCompleto.circ as structural Verilog
module contadorUnidades_0_9__circ (
  input  CLK,
  input  EN
);

  wire and_1_out, and_2_out, and_3_out, and_4_out, and_5_out, and_6_out, and_7_out, and_8_out, and_9_out,
       and_10_out, and_11_out, and_12_out, and_13_out, and_14_out, and_15_out, and_16_out, D0_q, D1_q, D2_q,
       D3_q, nand_1_out, not_1_out, not_2_out, not_3_out, not_4_out, not_5_out, not_6_out, not_7_out,
       not_8_out, not_9_out, not_10_out, not_11_out, not_12_out, or_1_out, or_2_out, or_3_out, or_4_out,
       or_5_out, or_6_out, or_7_out, xor_1_out;

  not not_1 (not_1_out, D2_q);
  not not_2 (not_2_out, D0_q);
  not not_3 (not_3_out, D3_q);
  not not_4 (not_4_out, D1_q);
  and and_1 (and_1_out, D3_q, not_1_out, not_4_out, not_2_out);
  and and_2 (and_2_out, not_3_out, D2_q, D1_q, D0_q);
  or or_1 (or_1_out, and_1_out, and_2_out);
  not not_5 (not_5_out, EN);
  D_Flip_Flop D3 (.clk(CLK), .D(or_2_out), .Q(D3_q));  // open: Qn, preset, en, reset
  not not_6 (not_6_out, D3_q);
  and and_3 (and_3_out, or_1_out, EN);
  or or_2 (or_2_out, and_3_out, and_4_out);
  and and_4 (and_4_out, D3_q, not_5_out);
  D_Flip_Flop D2 (.clk(CLK), .D(or_4_out), .Q(D2_q));  // open: Qn, preset, en, reset
  not not_7 (not_7_out, D2_q);
  nand nand_1 (nand_1_out, D1_q, D0_q);
  and and_5 (and_5_out, D2_q, nand_1_out);
  or or_3 (or_3_out, and_5_out, and_9_out);
  and and_6 (and_6_out, not_6_out, or_3_out);
  and and_7 (and_7_out, and_6_out, EN);
  and and_8 (and_8_out, D2_q, not_5_out);
  xor xor_1 (xor_1_out, D1_q, D0_q);
  and and_9 (and_9_out, not_7_out, D1_q, D0_q);
  or or_4 (or_4_out, and_7_out, and_8_out);
  D_Flip_Flop D1 (.clk(CLK), .D(or_5_out), .Q(D1_q));  // open: Qn, preset, en, reset
  not not_8 (not_8_out, D3_q);
  and and_10 (and_10_out, xor_1_out, not_8_out);
  and and_11 (and_11_out, and_10_out, EN);
  or or_5 (or_5_out, and_11_out, and_12_out);
  and and_12 (and_12_out, D1_q, not_5_out);
  D_Flip_Flop D0 (.clk(CLK), .D(or_7_out), .Q(D0_q));  // open: Qn, preset, en, reset
  not not_9 (not_9_out, D2_q);
  not not_10 (not_10_out, D1_q);
  and and_13 (and_13_out, not_9_out, not_10_out);
  not not_11 (not_11_out, D3_q);
  or or_6 (or_6_out, not_11_out, and_13_out);
  not not_12 (not_12_out, D0_q);
  and and_14 (and_14_out, or_6_out, not_12_out);
  and and_15 (and_15_out, and_14_out, EN);
  and and_16 (and_16_out, D0_q, not_5_out);
  or or_7 (or_7_out, and_15_out, and_16_out);
  main main_1 ();
endmodule

module contadorDezenas_0_5__circ (
  input  CLK,
  input  EN
);

  wire and_1_out, and_2_out, and_3_out, and_4_out, and_5_out, and_6_out, and_7_out, and_8_out, and_9_out,
       and_10_out, D0_q, D1_q, D2_q, not_1_out, not_2_out, not_3_out, not_4_out, not_5_out, not_6_out,
       not_7_out, not_8_out, or_1_out, or_2_out, or_3_out, or_4_out, or_5_out, xor_1_out;

  not not_1 (not_1_out, D2_q);
  not not_2 (not_2_out, EN);
  D_Flip_Flop D2 (.clk(CLK), .D(or_2_out), .Q(D2_q));  // open: Qn, preset, en, reset
  and and_1 (and_1_out, not_1_out, D1_q, D0_q);
  or or_1 (or_1_out, and_1_out, and_2_out);
  not not_3 (not_3_out, D0_q);
  not not_4 (not_4_out, D1_q);
  and and_2 (and_2_out, D2_q, not_4_out, not_3_out);
  and and_3 (and_3_out, or_1_out, EN);
  and and_4 (and_4_out, D2_q, not_2_out);
  D_Flip_Flop D1 (.clk(CLK), .D(or_4_out), .Q(D1_q));  // open: Qn, preset, en, reset
  not not_5 (not_5_out, D2_q);
  and and_5 (and_5_out, not_5_out, xor_1_out);
  or or_2 (or_2_out, and_3_out, and_4_out);
  not not_6 (not_6_out, D2_q);
  xor xor_1 (xor_1_out, D1_q, D0_q);
  or or_3 (or_3_out, not_6_out, not_7_out);
  and and_6 (and_6_out, and_5_out, EN);
  and and_7 (and_7_out, D1_q, not_2_out);
  D_Flip_Flop D0 (.clk(CLK), .D(or_5_out), .Q(D0_q));  // open: Qn, preset, en, reset
  not not_7 (not_7_out, D1_q);
  not not_8 (not_8_out, D0_q);
  and and_8 (and_8_out, or_3_out, not_8_out);
  and and_9 (and_9_out, and_8_out, EN);
  and and_10 (and_10_out, D0_q, not_2_out);
  or or_4 (or_4_out, and_6_out, and_7_out);
  or or_5 (or_5_out, and_9_out, and_10_out);
endmodule

module decodificadorA (
  input  B4,
  input  B3,
  input  B2,
  input  B1,
  output out_5
);

  wire xnor_1_out;

  xnor xnor_1 (xnor_1_out, B4, B2);
  or or_1 (out_5, xnor_1_out, B3, B1);
endmodule

module decodificadorB (
  input  B4,
  input  B3,
  input  B2,
  input  B1,
  output out_5
);

  wire not_1_out, xnor_1_out;

  xnor xnor_1 (xnor_1_out, B4, B3);
  not not_1 (not_1_out, B2);
  or or_1 (out_5, xnor_1_out, not_1_out);
endmodule

module decodificadorC (
  input  B4,
  input  B3,
  input  B2,
  input  B1,
  output out_5
);

  wire not_1_out;

  not not_1 (not_1_out, B3);
  or or_1 (out_5, B4, not_1_out, B2);
endmodule

module decodificadorD (
  input  B4,
  input  B3,
  input  B2,
  input  B1,
  output out_5
);

  wire and_1_out, and_2_out, and_3_out, and_4_out, not_1_out, not_2_out, not_3_out;

  not not_1 (not_1_out, B4);
  and and_1 (and_1_out, not_1_out, B3);
  not not_2 (not_2_out, B2);
  not not_3 (not_3_out, B3);
  and and_2 (and_2_out, not_1_out, not_2_out);
  and and_3 (and_3_out, not_2_out, B3);
  and and_4 (and_4_out, B2, not_3_out, B4);
  or or_1 (out_5, and_1_out, B1, and_2_out, and_3_out, and_4_out);
endmodule

module decodificadorE (
  input  B4,
  input  B3,
  input  B2,
  input  B1,
  output out_5
);

  wire and_1_out, and_2_out, not_1_out, not_2_out;

  not not_1 (not_1_out, B4);
  not not_2 (not_2_out, B2);
  and and_1 (and_1_out, not_1_out, not_2_out);
  and and_2 (and_2_out, not_1_out, B3);
  or or_1 (out_5, and_1_out, and_2_out);
endmodule

module decodificadorF (
  input  B4,
  input  B3,
  input  B2,
  input  B1,
  output out_5
);

  wire and_1_out, and_2_out, and_3_out, not_1_out, not_2_out;

  not not_1 (not_1_out, B4);
  not not_2 (not_2_out, B3);
  and and_1 (and_1_out, not_1_out, B2);
  and and_2 (and_2_out, not_1_out, not_2_out);
  and and_3 (and_3_out, B2, not_2_out);
  or or_1 (out_5, and_1_out, and_2_out, and_3_out, B1);
endmodule

module decodificadorG (
  input  B4,
  input  B3,
  input  B2,
  input  B1,
  output out_5
);

  wire and_1_out, not_1_out, xor_1_out;

  not not_1 (not_1_out, B4);
  xor xor_1 (xor_1_out, B3, B2);
  and and_1 (and_1_out, B2, not_1_out);
  or or_1 (out_5, and_1_out, xor_1_out, B1);
endmodule

module decodificadorBCD (
  input  D,
  input  C,
  input  B,
  input  A,
  output A_2,
  output B_2,
  output C_2,
  output D_2,
  output E,
  output F,
  output G
);

  decodificadorA decodificadora_1 (.B4(D), .B3(C), .B2(B), .B1(A), .out_5(A_2));
  decodificadorB decodificadorb_1 (.B4(D), .B3(C), .B2(B), .B1(A), .out_5(B_2));
  decodificadorC decodificadorc_1 (.B4(D), .B3(C), .B2(B), .B1(A), .out_5(C_2));
  decodificadorD decodificadord_1 (.B4(D), .B3(C), .B2(B), .B1(A), .out_5(D_2));
  decodificadorE decodificadore_1 (.B4(D), .B3(C), .B2(B), .B1(A), .out_5(E));
  decodificadorF decodificadorf_1 (.B4(D), .B3(C), .B2(B), .B1(A), .out_5(F));
  decodificadorG decodificadorg_1 (.B4(D), .B3(C), .B2(B), .B1(A), .out_5(G));
endmodule

module contadorHoras (
  input  EN,
  input  U0,
  input  U1,
  input  U2,
  input  U3,
  input  T0,
  input  T1,
  input  CLK
);

  wire and_3_out, and_4_out, and_5_out, and_6_out, and_7_out, and_8_out, and_9_out, and_10_out, and_11_out,
       and_12_out, and_13_out, FF_T0_q, FF_T1_q, FF_U0_q, FF_U1_q, FF_U2_q, FF_U3_q, last, nine, notw,
       or_1_out, or_2_out, xor_1_out, xor_2_out, xor_3_out, xor_4_out, xor_5_out, xor_6_out;

  and and_1 (nine, U3, U0);
  and and_2 (last, T1, U1, U0);
  or or_1 (or_1_out, nine, last);
  and and_3 (and_3_out, nine, T0);
  and and_4 (and_4_out, EN, nine);
  and and_5 (and_5_out, EN, U0, U1, U2);
  and and_6 (and_6_out, EN, U0, U1);
  and and_7 (and_7_out, EN, U0);
  and and_8 (and_8_out, EN, or_1_out);
  or or_2 (or_2_out, and_3_out, last);
  xor xor_1 (xor_1_out, and_4_out, T0);
  xor xor_2 (xor_2_out, and_5_out, U3);
  xor xor_3 (xor_3_out, and_6_out, U2);
  xor xor_4 (xor_4_out, and_7_out, U1);
  xor xor_5 (xor_5_out, EN, U0);
  not not_1 (notw, and_8_out);
  and and_9 (and_9_out, xor_2_out, notw);
  and and_10 (and_10_out, xor_3_out, notw);
  and and_11 (and_11_out, xor_4_out, notw);
  and and_12 (and_12_out, xor_5_out, notw);
  and and_13 (and_13_out, EN, or_2_out);
  xor xor_6 (xor_6_out, and_13_out, T1);
  D_Flip_Flop FF_T1 (.clk(CLK), .D(xor_6_out), .Q(FF_T1_q));  // open: Qn, preset, en, reset
  D_Flip_Flop FF_T0 (.clk(CLK), .D(xor_1_out), .Q(FF_T0_q));  // open: Qn, preset, en, reset
  D_Flip_Flop FF_U3 (.clk(CLK), .D(and_9_out), .Q(FF_U3_q));  // open: Qn, preset, en, reset
  D_Flip_Flop FF_U2 (.clk(CLK), .D(and_10_out), .Q(FF_U2_q));  // open: Qn, preset, en, reset
  D_Flip_Flop FF_U1 (.clk(CLK), .D(and_11_out), .Q(FF_U1_q));  // open: Qn, preset, en, reset
  D_Flip_Flop FF_U0 (.clk(CLK), .D(and_12_out), .Q(FF_U0_q));  // open: Qn, preset, en, reset
endmodule

module mod10 (
  input  EN,
  input  UP,
  input  U0,
  input  U1,
  input  U2,
  input  U3
);

  wire clrA, clrB, CO, keepA, keepB, nUP, tog1, tog2, tog3, wdn, wup, xor_1_out, xor_2_out, xor_3_out,
       xor_4_out, xor_5_out, xor_6_out, zero;

  not not_1 (nUP, UP);
  not not_2 (keepA, clrA);
  xor xor_1 (xor_1_out, U0, nUP);
  xor xor_2 (xor_2_out, U1, nUP);
  xor xor_3 (xor_3_out, U2, nUP);
  nor nor_1 (zero, U0, U1, U2, U3);
  and and_1 (wup, UP, U3, U0);
  and and_2 (wdn, zero, nUP);
  or or_1 (CO, wup, wdn);
  and and_3 (clrA, EN, wup);
  and and_4 (clrB, EN, wdn);
  nor nor_2 (keepB, clrA, clrB);
  // AND_Gate and_5 has open pins: in0=keepA, in1=xor_4_out, out=open
  xor xor_4 (xor_4_out, tog2, U3);
  // AND_Gate and_6 has open pins: in0=keepB, in1=xor_5_out, out=open
  xor xor_5 (xor_5_out, tog1, U2);
  buf xor_6 (xor_6_out, U1);  // XOR_Gate
  and and_7 (tog1, xor_1_out, EN);
  and and_8 (tog2, xor_2_out, tog1);
  and and_9 (tog3, xor_3_out, tog2);
  // AND_Gate and_10 has open pins: in0=keepB, in1=xor_6_out, out=open
endmodule
